# Fritzing sketch file25 (saved by Fritzing 0.9.4)
breadboards: 1

parts:
  J1 = Piezo Speaker
  S1 = Pushbutton [package="[THT]"]
  Part1 = Arduino Uno (Rev3)

nets:
  N1: J1.pin1, S1.Pin_3, S1.Pin_4, Part1.GND
  N2: J1.pin2, Part1.D9_PWM
  N3: S1.Pin_1, S1.Pin_2, Part1.RESET
